// Logisim project memory.circ as structural Verilog: 1 circuit, main circuit main
module main (
  input  nY0W,
  input  [7:0] DATA,
  input  nWR,
  input  nMREQ,
  input  nRD,
  input  [15:0] ADDRESS
);

  wire A16, A16_q, A17, A17_q, A18, A18_q, not_1_out, not_2_out, not_3_out, not_4_out, not_5_out, not_6_out,
       not_7_out, not_8_out, nRAM_CE, nROM_CE, or_1_out, or_2_out, or_3_out, or_4_out, RAM_ONLY_q;
  wire [12:0] bit_extender_1_out;

  not not_1 (not_1_out, nY0W);
  D_Flip_Flop u_A16 (.clk(not_1_out), .D(DATA[0]), .Q(A16_q));  // open: Qn, preset, en, reset
  D_Flip_Flop u_A17 (.clk(not_1_out), .D(DATA[1]), .Q(A17_q));  // open: Qn, preset, en, reset
  D_Flip_Flop u_A18 (.clk(not_1_out), .D(DATA[2]), .Q(A18_q));  // open: Qn, preset, en, reset
  D_Flip_Flop RAM_ONLY (.clk(not_1_out), .D(DATA[3]), .Q(RAM_ONLY_q));  // open: Qn, preset, en, reset
  not not_2 (not_2_out, RAM_ONLY_q);
  // Probe on not_2_out
  // Probe on ADDRESS[15]
  // Probe on ADDRESS[14]
  // Probe on ADDRESS[13]
  or or_1 (or_1_out, nWR, nMREQ);
  or or_2 (or_2_out, nMREQ, nRD);
  Bit_Extender #(.in_width(16), .out_width(13)) bit_extender_1 (.in(ADDRESS), .out(bit_extender_1_out));
  or or_3 (or_3_out, ADDRESS[15], ADDRESS[14]);
  not not_3 (not_3_out, nRAM_CE);
  not not_4 (not_4_out, or_1_out);
  not not_5 (not_5_out, or_2_out);
  not not_6 (not_6_out, nROM_CE);
  not not_7 (not_7_out, or_2_out);
  or or_4 (or_4_out, or_3_out, ADDRESS[13]);
  not not_8 (not_8_out, or_4_out);
  RAM #(.addrWidth(19)) ram_1 (
    .addr({A18, A17, A16, ADDRESS}), .data(DATA), .sel(not_3_out), .clk(not_4_out), .ld(not_5_out));  // open: clr
  RAM #(.addrWidth(13)) ram_2 (
    .addr(bit_extender_1_out), .data(DATA), .sel(not_6_out), .clk(1'b0), .ld(not_7_out));  // open: clr
  // Probe on A16_q
  // Probe on A17_q
  // Probe on A18_q
  and and_1 (nRAM_CE, not_2_out, not_8_out);
  not not_9 (nROM_CE, nRAM_CE);
  and and_2 (A16, or_3_out, A16_q);
  and and_3 (A17, or_3_out, A17_q);
  and and_4 (A18, or_3_out, A18_q);

  // Other names for the same wires on the sheet: ADDR[15:0] = ADDRESS

  // Notes on the sheet:
  //   nRD: pull=up
  //   ADDRESS: pull=down
  //   nY0W: pull=up
  //   nMREQ: pull=up
  //   DATA: pull=down
  //   nWR: pull=up
  //   Use RAM if < 8k
  //   RAM
  //   ROM
  //   Use ROM
  //   Use RAM
endmodule
